# Fritzing sketch door-monitor (saved by Fritzing 0.9.3b)
circuit board: 3.18916cm x 3.64065cm
breadboards: 1

parts:
  U1 = ESP8266 WiFi Module [part_number=ESP8266]
  R1 = Resistor [tolerance=±5% resistance=4.7k package=THT]
  R2 = Resistor [tolerance=±5% resistance=4.7k package=THT]
  R3 = Resistor [tolerance=±5% resistance=4.7k package=THT]
  S1 = Toggle Switch [package=THT]
  VCC1 = Battery

nets:
  N1: U1.VCC, R1.Pin_0, R2.Pin_0, R3.Pin_0, VCC1.+
  N2: U1.GPIO_0, R3.Pin_1, S1.COM
  N3: U1.RST, U1.CH_PD, R1.Pin_1
  N4: U1.GPIO_2, R2.Pin_1, S1.L1
  N5: U1.GND, VCC1.-

custom parts:
  ESP8266 WiFi Module: Generic WiFi Module based on the ESP8266 with onboard PCB antenna and UART communications
